# Fritzing sketch Game Console Schematic Diagram (saved by Fritzing 0.9.3b)
breadboards: 1

parts:
  LED5 = LED - 5mm [color="Green (555nm)" package="5 mm [THT]"]
  R1 = Resistor [tolerance=±5% resistance=2k package=THT]
  Part1 = Arduino Due (Rev2b)
  R2 = Resistor [tolerance=±5% resistance=2k package=THT]
  LED6 = LED - 5mm [color="Green (555nm)" package="5 mm [THT]"]
  LED7 = LED - 5mm [color="Green (555nm)" package="5 mm [THT]"]
  LED8 = LED - 5mm [color="Green (555nm)" package="5 mm [THT]"]
  LED9 = LED - 5mm [color="Green (555nm)" package="5 mm [THT]"]
  LED10 = LED - 5mm [color="Yellow (595nm)" package="5 mm [THT]"]
  LED11 = LED - 5mm [color="Yellow (595nm)" package="5 mm [THT]"]
  LED12 = LED - 5mm [color="Yellow (595nm)" package="5 mm [THT]"]
  LED13 = LED - 5mm [color="Yellow (595nm)" package="5 mm [THT]"]
  LED14 = LED - 5mm [color="Yellow (595nm)" package="5 mm [THT]"]
  R3 = Resistor [tolerance=±5% resistance=2k package=THT]
  LED15 = LED - 5mm [color="Red (633nm)" package="5 mm [THT]"]
  LED16 = LED - 5mm [color="Red (633nm)" package="5 mm [THT]"]
  LED17 = LED - 5mm [color="Red (633nm)" package="5 mm [THT]"]
  LED18 = LED - 5mm [color="Red (633nm)" package="5 mm [THT]"]
  LED19 = LED - 5mm [color="Red (633nm)" package="5 mm [THT]"]
  R5 = Resistor [tolerance=±5% resistance=2k package=THT]
  LED20 = LED - 5mm [color="Blue (470nm)" package="5 mm [THT]"]
  R7 = Resistor [tolerance=±5% resistance=2k package=THT]
  LED21 = LED - 5mm [color="Blue (470nm)" package="5 mm [THT]"]
  LED22 = LED - 5mm [color="Blue (470nm)" package="5 mm [THT]"]
  LED23 = LED - 5mm [color="Blue (470nm)" package="5 mm [THT]"]
  LED24 = LED - 5mm [color="Blue (470nm)" package="5 mm [THT]"]
  R8 = Resistor [tolerance=±5% resistance=2k package=THT]
  LED25 = LED - 5mm [color="White (4500K)" package="5 mm [THT]"]
  LED26 = LED - 5mm [color="White (4500K)" package="5 mm [THT]"]
  LED27 = LED - 5mm [color="White (4500K)" package="5 mm [THT]"]
  LED28 = LED - 5mm [color="White (4500K)" package="5 mm [THT]"]
  LED29 = LED - 5mm [color="White (4500K)" package="5 mm [THT]"]
  R9 = Resistor [tolerance=±5% resistance=2k package=THT]
  R10 = Resistor [tolerance=±5% resistance=2k package=THT]
  Piezo_Buzzer = Piezo Speaker
  R11 = Resistor [tolerance=±5% resistance=100 package=THT]
  LCD1 = LCD screen
  R6 = Resistor [tolerance=±5% resistance=2k package=THT]
  R4 = Resistor [tolerance=±5% resistance=2k package=THT]
  R12 = Resistor [tolerance=±5% resistance=220 package=THT]
  R13 = Trimmer Potentiometer [maximum_resistance=10kΩ package=THT]
  S1 = Pushbutton [package="[THT]"]
  S2 = Pushbutton [package="[THT]"]
  S3 = Pushbutton [package="[THT]"]
  S4 = Pushbutton [package="[THT]"]
  S5 = Pushbutton [package="[THT]"]
  R14 = Resistor [tolerance=±5% resistance=10 package=THT]
  R15 = Resistor [tolerance=±5% resistance=1k package=THT]
  R16 = Resistor [tolerance=±5% resistance=1k package=THT]
  R17 = Resistor [tolerance=±5% resistance=10 package=THT]
  R18 = Resistor [tolerance=±5% resistance=10 package=THT]
  R19 = Resistor [tolerance=±5% resistance=1k package=THT]
  R20 = Resistor [tolerance=±5% resistance=10 package=THT]
  R21 = Resistor [tolerance=±5% resistance=1k package=THT]
  R22 = Resistor [tolerance=±5% resistance=10 package=THT]
  R23 = Resistor [tolerance=±5% resistance=1k package=THT]

nets:
  N1: LED5.cathode, R1.Pin_0, LED6.cathode, LED7.cathode
  N2: LED5.anode, Part1.D42
  GND: R1.Pin_1, Part1.GND, R2.Pin_0, R3.Pin_0, R5.Pin_1, R7.Pin_1, R8.Pin_1, R9.Pin_1, R10.Pin_1, R11.Pin_1, LCD1.VSS, LCD1.R/W, LCD1.LED-, R6.Pin_1, R4.Pin_0, R13.leg1, R14.Pin_0, R15.Pin_0, R16.Pin_1, R19.Pin_0, R21.Pin_1, R23.Pin_1
  N3: Part1.A2, S1.Pin_1, S1.Pin_2, R16.Pin_0
  N4: Part1.A3, S3.Pin_1, S3.Pin_2, R19.Pin_1
  N5: Part1.A4, S4.Pin_1, S4.Pin_2, R15.Pin_1
  N6: Part1.A5, S5.Pin_1, S5.Pin_2, R23.Pin_0
  N7: Part1.A6, S2.Pin_1, S2.Pin_2, R21.Pin_0
  N8: Part1.D14/TX3, LCD1.DB5
  N9: Part1.D15/RX3, LCD1.DB6
  N10: Part1.D16/TX2, LCD1.DB7
  5V: Part1.5V, LCD1.VDD, R12.Pin_1, R13.leg2, R17.Pin_1, R18.Pin_1, R20.Pin_1, R22.Pin_1
  N11: Part1.D8_PWM, Piezo_Buzzer.pin2
  N12: Part1.D11_PWM, LCD1.RS
  N13: Part1.D12_PWM, LCD1.E
  N14: Part1.D13_PWM, LCD1.DB4
  N15: Part1.D22, LED9.anode
  N16: Part1.D23, LED14.anode
  N17: Part1.D24, LED19.anode
  N18: Part1.D25, LED20.anode
  N19: Part1.D26, LED29.anode
  N20: Part1.D27, LED8.anode
  N21: Part1.D28, LED13.anode
  N22: Part1.D29, LED18.anode
  N23: Part1.D30, LED21.anode
  N24: Part1.D31, LED28.anode
  N25: Part1.D32, LED7.anode
  N26: Part1.D33, LED12.anode
  N27: Part1.D34, LED17.anode
  N28: Part1.D35, LED22.anode
  N29: Part1.D36, LED27.anode
  N30: Part1.D37, LED6.anode
  N31: Part1.D38, LED11.anode
  N32: Part1.D39, LED16.anode
  N33: Part1.D40, LED23.anode
  N34: Part1.D41, LED26.anode
  N35: Part1.D43, LED10.anode
  N36: Part1.D44, LED15.anode
  N37: Part1.D45, LED24.anode
  N38: Part1.D46, LED25.anode
  N39: R2.Pin_1, LED8.cathode, LED9.cathode
  N40: LED10.cathode, LED11.cathode, R4.Pin_1
  N41: LED12.cathode, LED13.cathode, LED14.cathode, R3.Pin_1
  N42: LED15.cathode, LED16.cathode, LED17.cathode, R6.Pin_0
  N43: LED18.cathode, LED19.cathode, R5.Pin_0
  N44: LED20.cathode, R7.Pin_0, LED21.cathode, LED22.cathode
  N45: LED23.cathode, LED24.cathode, R8.Pin_0
  N46: LED25.cathode, LED26.cathode, LED27.cathode, R10.Pin_0
  N47: LED28.cathode, LED29.cathode, R9.Pin_0
  N48: Piezo_Buzzer.pin1, R11.Pin_0
  N49: LCD1.V0, R13.wiper
  N50: LCD1.LED+, R12.Pin_0
  N51: S1.Pin_3, S1.Pin_4, R17.Pin_0
  N52: S2.Pin_3, S2.Pin_4, R20.Pin_0
  N53: S3.Pin_3, S3.Pin_4, R22.Pin_0
  N54: S4.Pin_3, S4.Pin_4, R14.Pin_1
  N55: S5.Pin_3, S5.Pin_4, R18.Pin_0
